# Fritzing sketch PamsLightSwitch (saved by Fritzing 1.0.5)
circuit board: 8.46667cm x 5.64444cm

parts:
  part = HLK-PM01
  KY-019_Relay = KY-019 5V Relay Module [package="Breakout board"]
  DS-1302_Clock = MH Sensor RTC Module2
  NanoEveryman_Arduino = Arduino Nano Every

nets:
  GND: part.-Vo, KY-019_Relay.-, DS-1302_Clock.GND, NanoEveryman_Arduino.GND
  N1: part.+Vo, KY-019_Relay.+, NanoEveryman_Arduino.VIN
  N2: KY-019_Relay.S, NanoEveryman_Arduino.D6~
  VCC: DS-1302_Clock.VCC, NanoEveryman_Arduino.D11/MOSI, NanoEveryman_Arduino.+5V
  N3: DS-1302_Clock.CLK, NanoEveryman_Arduino.D8
  N4: DS-1302_Clock.DAT, NanoEveryman_Arduino.D4
  N5: DS-1302_Clock.RST, NanoEveryman_Arduino.D2

custom parts:
  HLK-PM01: AC-DC 220V to 5V Step-Down Power Supply Module
  KY-019 5V Relay Module: KY-019 5V Relay module, used to control AC circuits. (Special thanks to vanepp for fixing the PCB holes and other errors)
  MH Sensor RTC Module2: Arduino module DS1302 SPI Real Time Clock
  Arduino Nano Every: The Nano Every is Arduino’s 5V compatible board in the smallest available form factor: 45x18mm! The Arduino Nano is the preferred board for many projects requiring a small and easy to use microcontroller board. The small footprint and low price, make the Nano Every particularly suited for wearable inventions, low cost robotics, electronic musical instruments, and general use to control smaller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
